// Logisim project alu.circ as structural Verilog: 1 circuit, main circuit alu
module alu (
  input  [31:0] A,
  input  [31:0] B,
  input  [3:0] ALUSel,
  output [31:0] Result
);

  wire comparator_1_eq, comparator_2_eq, comparator_3_eq, comparator_4_lt;
  wire [4:0] bit_extender_6_out, bit_extender_7_out, bit_extender_8_out;
  wire [5:0] bitadder_1_out, bitadder_2_out;
  wire [31:0] adder_3_out, ALU_ADD, ALU_AND, ALU_CNTO, ALU_DIVU, ALU_MULH, ALU_MULHU, ALU_MULT, ALU_OR,
       ALU_REMU, ALU_SIR, ALU_SLL, ALU_SLT, ALU_SRA, ALU_SRL, ALU_SUB, ALU_XOR, bit_extender_1_out,
       bit_extender_2_out, bit_extender_3_out, bit_extender_4_out, divider_1_out, divider_2_rem,
       multiplier_3_cout, multiplier_4_out, multiplier_5_out;

  assign ALU_AND = A & B;  // AND_Gate and_1, 32 bits wide
  assign ALU_OR = A | B;  // OR_Gate or_1, 32 bits wide
  assign ALU_XOR = A ^ B;  // XOR_Gate xor_1, 32 bits wide
  BitAdder #(.width(1)) bitadder_1 (
    .in0(A[0]), .in1(A[1]), .in2(A[2]), .in3(A[3]), .in4(A[4]), .in5(A[5]), .in6(A[6]), .in7(A[7]),
    .in8(A[8]), .in9(A[9]), .in10(A[10]), .in11(A[11]), .in12(A[12]), .in13(A[13]), .in14(A[14]),
    .in15(A[15]), .in16(A[16]), .in17(A[17]), .in18(A[18]), .in19(A[19]), .in20(A[20]), .in21(A[21]),
    .in22(A[22]), .in23(A[23]), .in24(A[24]), .in25(A[25]), .in26(A[26]), .in27(A[27]), .in28(A[28]),
    .in29(A[29]), .in30(A[30]), .in31(A[31]), .out(bitadder_1_out));
  BitAdder #(.width(1)) bitadder_2 (
    .in0(B[0]), .in1(B[1]), .in2(B[2]), .in3(B[3]), .in4(B[4]), .in5(B[5]), .in6(B[6]), .in7(B[7]),
    .in8(B[8]), .in9(B[9]), .in10(B[10]), .in11(B[11]), .in12(B[12]), .in13(B[13]), .in14(B[14]),
    .in15(B[15]), .in16(B[16]), .in17(B[17]), .in18(B[18]), .in19(B[19]), .in20(B[20]), .in21(B[21]),
    .in22(B[22]), .in23(B[23]), .in24(B[24]), .in25(B[25]), .in26(B[26]), .in27(B[27]), .in28(B[28]),
    .in29(B[29]), .in30(B[30]), .in31(B[31]), .out(bitadder_2_out));
  assign bit_extender_1_out = {{26{1'b0}}, bitadder_1_out};  // Bit_Extender bit_extender_1
  assign bit_extender_2_out = {{26{1'b0}}, bitadder_2_out};  // Bit_Extender bit_extender_2
  Adder #(.width(32)) adder_1 (.a(A), .b(B), .out(ALU_ADD));  // open: cin, cout
  Subtractor #(.width(32)) subtractor_1 (.a(A), .b(B), .out(ALU_SUB));  // open: bin, bout
  Multiplier #(.width(32)) multiplier_1 (.a(A), .b(B), .out(ALU_MULT));  // open: cin, cout
  Multiplier #(.width(32)) multiplier_2 (.a(A), .b(B), .cout(ALU_MULHU));  // open: out, cin
  Adder #(.width(32)) adder_2 (.a(bit_extender_1_out), .b(bit_extender_2_out), .out(ALU_CNTO));  // open: cin, cout
  Multiplexer #(.select(4), .width(32), .enable("false")) multiplexer_1 (
    .in0(ALU_AND), .in1(ALU_OR), .in2(ALU_XOR), .in3(ALU_ADD), .in4(ALU_SUB), .in5(ALU_MULT),
    .in6(ALU_MULHU), .in7(ALU_MULH), .in8(ALU_DIVU), .in9(ALU_REMU), .in10(ALU_SRL), .in11(ALU_SRA),
    .in12(ALU_SLL), .in13(ALU_SLT), .in14(A), .in15(B), .out(Result), .sel(ALUSel));
  Divider #(.width(32)) divider_1 (.a(A), .b(B), .out(divider_1_out));  // open: upper, rem
  Divider #(.width(32)) divider_2 (.a(A), .b(B), .rem(divider_2_rem));  // open: out, upper
  Multiplier #(.width(32)) multiplier_3 (.a(A), .b(B), .cout(multiplier_3_cout));  // open: out, cin
  Multiplexer #(.width(32), .enable("false")) multiplexer_2 (
    .in0(divider_1_out), .in1(A), .out(ALU_DIVU), .sel(comparator_1_eq));
  Comparator #(.width(32)) comparator_1 (.a(B), .b({32{1'b0}}), .eq(comparator_1_eq));  // open: gt, lt
  Multiplexer #(.width(32), .enable("false")) multiplexer_3 (
    .in0(divider_2_rem), .in1(A), .out(ALU_REMU), .sel(comparator_2_eq));
  Comparator #(.width(32)) comparator_2 (.a(B), .b({32{1'b0}}), .eq(comparator_2_eq));  // open: gt, lt
  assign bit_extender_3_out = {{31{A[31]}}, A[31]};  // Bit_Extender bit_extender_3
  assign bit_extender_4_out = {{31{B[31]}}, B[31]};  // Bit_Extender bit_extender_4
  Multiplier #(.width(32)) multiplier_4 (.a(B), .b(bit_extender_3_out), .out(multiplier_4_out));  // open: cin, cout
  Comparator #(.width(32)) comparator_3 (
    .a({A[0], A[1], A[2], A[3], A[4], A[5], A[6], A[7], A[8], A[9], A[10], A[11], A[12], A[13], A[14], A[15], A[16], A[17], A[18], A[19], A[20], A[21], A[22], A[23], A[24], A[25], A[26], A[27], A[28], A[29], A[30], A[31]}),
    .b(B), .eq(comparator_3_eq));  // open: gt, lt
  Multiplier #(.width(32)) multiplier_5 (.a(A), .b(bit_extender_4_out), .out(multiplier_5_out));  // open: cin, cout
  assign ALU_SIR = {{31{1'b0}}, comparator_3_eq};  // Bit_Extender bit_extender_5
  Adder #(.width(32)) adder_3 (.a(multiplier_5_out), .b(multiplier_4_out), .out(adder_3_out));  // open: cin, cout
  Shifter #(.width(32), .shift("lr")) shifter_1 (.in(A), .\dist (bit_extender_6_out), .out(ALU_SRL));
  Bit_Extender #(.in_width(32), .out_width(5), .\type ("zero")) bit_extender_6 (.in(B), .out(bit_extender_6_out));
  Shifter #(.width(32), .shift("ar")) shifter_2 (.in(A), .\dist (bit_extender_7_out), .out(ALU_SRA));
  Bit_Extender #(.in_width(32), .out_width(5), .\type ("zero")) bit_extender_7 (.in(B), .out(bit_extender_7_out));
  Shifter #(.width(32)) shifter_3 (.in(A), .\dist (bit_extender_8_out), .out(ALU_SLL));
  Bit_Extender #(.in_width(32), .out_width(5), .\type ("zero")) bit_extender_8 (.in(B), .out(bit_extender_8_out));
  Adder #(.width(32)) adder_4 (.a(multiplier_3_cout), .b(adder_3_out), .out(ALU_MULH));  // open: cin, cout
  Comparator #(.width(32)) comparator_4 (.a(A), .b(B), .lt(comparator_4_lt));  // open: gt, eq
  assign ALU_SLT = {{31{1'b0}}, comparator_4_lt};  // Bit_Extender bit_extender_9

  // Other names for the same wires on the sheet: ALU_A[31:0] = A; ALU_B[31:0] = B

  // Notes on the sheet:
  //   INPUTS to your circuit
  //   DON'T CHANGE THE LOCATIONS OF THE INPUTS AND OUTPUTS!
  //   OUTPUT from your circuit
endmodule
