// Logisim project cpu.circ as structural Verilog: 4 circuits, main circuit main
module main (
  input  [31:0] INSTRUCTION,
  input  CLOCK,
  output [31:0] FETCH_ADDRESS,
  output [31:0] ra,
  output [31:0] sp,
  output [31:0] t0,
  output [31:0] t1,
  output [31:0] t2,
  output [31:0] s0,
  output [31:0] s1,
  output [31:0] a0
);

  wire Asel, Auipc, B_load, BrEq, BrLT, BrUn, Bsel, H_load, Kill, PCSel, RegWEn, U_load;
  wire [1:0] MemRW, WBSel;
  wire [2:0] ImmSel;
  wire [3:0] ALUSel;
  wire [31:0] alu_result, bit_extender_1_out, bit_extender_2_out, bit_extender_3_out, bit_extender_4_out,
       Data, DataRead, Imm, INSTRUCTION_pipe, multiplexer_1_out, multiplexer_2_out, multiplexer_3_out,
       multiplexer_4_out, multiplexer_5_out, multiplexer_6_out, multiplexer_7_out, multiplexer_8_out,
       multiplexer_9_out, multiplexer_11_out, multiplexer_12_out, PC_pipe, PC_pipe_4, PC_plus_4, r1, r2,
       shifter_1_out, shifter_2_out, shifter_3_out, shifter_4_out, wd;

  // Probe on alu_result
  Multiplexer #(.width(32), .enable("false")) multiplexer_1 (
    .in0(PC_plus_4), .in1(alu_result), .out(multiplexer_1_out), .sel(PCSel));
  Register #(.width(32)) register_1 (.D(multiplexer_1_out), .en(1'b1), .clk(CLOCK), .Q(FETCH_ADDRESS));  // open: clr
  Control control_1 (
    .Inst(INSTRUCTION_pipe), .BrEq(BrEq), .BrLT(BrLT), .PCSel(PCSel), .ImmSel(ImmSel), .ALUSel(ALUSel),
    .RegWEn(RegWEn), .MemRW(MemRW), .BrUn(BrUn), .WBSel(WBSel), .ASel(Asel), .BSel(Bsel), .kill(Kill),
    .Auipc(Auipc), .B_load(B_load), .H_load(H_load), .U_load(U_load));
  Adder #(.width(32)) adder_1 (.a(FETCH_ADDRESS), .b(32'h1), .out(PC_plus_4));  // open: cin, cout
  // Probe on INSTRUCTION
  Register #(.width(32)) register_2 (.D(FETCH_ADDRESS), .en(1'b1), .clk(CLOCK), .Q(PC_pipe));  // open: clr
  Register #(.width(32)) register_3 (.D(multiplexer_2_out), .en(1'b1), .clk(CLOCK), .Q(INSTRUCTION_pipe));  // open: clr
  Multiplexer #(.width(32), .enable("false")) multiplexer_2 (
    .in0(INSTRUCTION), .in1(32'h13), .out(multiplexer_2_out), .sel(Kill));
  // Probe on INSTRUCTION_pipe
  Imm_Gen imm_gen_1 (.Instruction(INSTRUCTION_pipe), .ImmSel(ImmSel), .Imm(Imm));
  regfile_main RegFile (
    .rs2(INSTRUCTION_pipe[24:20]), .rd(INSTRUCTION_pipe[11:7]), .Read_Data_1(r1), .Read_Data_2(r2), .ra(ra),
    .sp(sp), .t0(t0), .t1(t1), .t2(t2), .s0(s0), .s1(s1), .a0(a0), .rs1(INSTRUCTION_pipe[19:15]),
    .Write_Data(wd), .RegWEn(RegWEn), .clk(CLOCK));
  Adder #(.width(32)) adder_2 (.a(PC_pipe), .b(32'h1), .out(PC_pipe_4));  // open: cin, cout
  Branch_Comp branch_comp_1 (.r1(r1), .r2(r2), .BrUn(BrUn), .BrEq(BrEq), .BrLT(BrLT));
  Multiplexer #(.width(32), .enable("false")) multiplexer_3 (
    .in0(r1), .in1(shifter_1_out), .out(multiplexer_3_out), .sel(Kill));
  Shifter #(.width(32), .shift("ar")) shifter_1 (.in(r1), .\dist (5'b00010), .out(shifter_1_out));
  Multiplexer #(.width(32), .enable("false")) multiplexer_4 (
    .in0(PC_pipe), .in1(shifter_2_out), .out(multiplexer_4_out), .sel(Auipc));
  Shifter #(.width(32)) shifter_2 (.in(PC_pipe), .\dist (5'b00010), .out(shifter_2_out));
  Shifter #(.width(32), .shift("ar")) shifter_3 (.in(Imm), .\dist (5'b00010), .out(shifter_3_out));
  Multiplexer #(.width(32), .enable("false")) multiplexer_5 (
    .in0(Imm), .in1(shifter_3_out), .out(multiplexer_5_out), .sel(Kill));
  Multiplexer #(.width(32), .enable("false")) multiplexer_6 (
    .in0(multiplexer_3_out), .in1(multiplexer_4_out), .out(multiplexer_6_out), .sel(Asel));
  Multiplexer #(.width(32), .enable("false")) multiplexer_7 (
    .in0(r2), .in1(multiplexer_5_out), .out(multiplexer_7_out), .sel(Bsel));
  // Probe on multiplexer_5_out
  // Probe on alu_result
  alu Arithmetic_Logic_Unit (.A(multiplexer_6_out), .B(multiplexer_7_out), .ALUSel(ALUSel), .Result(alu_result));
  mem_main DMEM (.WriteAddr(alu_result), .MemRW(MemRW), .clk(CLOCK), .WriteData(r2), .ReadData(DataRead));
  assign bit_extender_1_out = {{16{DataRead[15]}}, DataRead[15:0]};  // Bit_Extender bit_extender_1
  assign bit_extender_2_out = {{16{1'b0}}, DataRead[15:0]};  // Bit_Extender bit_extender_2
  Multiplexer #(.width(32), .enable("false")) multiplexer_8 (
    .in0(bit_extender_1_out), .in1(bit_extender_2_out), .out(multiplexer_8_out), .sel(U_load));
  Multiplexer #(.width(32), .enable("false")) multiplexer_9 (
    .in0(DataRead), .in1(multiplexer_8_out), .out(multiplexer_9_out), .sel(H_load));
  assign bit_extender_3_out = {{24{DataRead[7]}}, DataRead[7:0]};  // Bit_Extender bit_extender_3
  assign bit_extender_4_out = {{24{1'b0}}, DataRead[7:0]};  // Bit_Extender bit_extender_4
  Multiplexer #(.width(32), .enable("false")) multiplexer_10 (
    .in0(multiplexer_9_out), .in1(multiplexer_11_out), .out(Data), .sel(B_load));
  Multiplexer #(.width(32), .enable("false")) multiplexer_11 (
    .in0(bit_extender_3_out), .in1(bit_extender_4_out), .out(multiplexer_11_out), .sel(U_load));
  Multiplexer #(.select(2), .width(32), .enable("false")) multiplexer_12 (
    .in0(Data), .in1(alu_result), .in2(PC_pipe_4), .out(multiplexer_12_out), .sel(WBSel));  // open: in3
  // Probe on multiplexer_12_out
  Multiplexer #(.width(32), .enable("false")) multiplexer_13 (
    .in0(multiplexer_12_out), .in1(shifter_4_out), .out(wd), .sel(Kill));
  Shifter #(.width(32)) shifter_4 (.in(multiplexer_12_out), .\dist (5'b00010), .out(shifter_4_out));

  // Other names for the same wires on the sheet: clk = CLOCK; fetch_addr[31:0] = FETCH_ADDRESS;
  //   PC[31:0] = FETCH_ADDRESS; rd[4:0] = INSTRUCTION_pipe[11:7]; rs1[4:0] = INSTRUCTION_pipe[19:15];
  //   rs2[4:0] = INSTRUCTION_pipe[24:20]

  // Notes on the sheet:
  //   Output
  //   Inputs/Outputs from run.circ. DO NOT MOVE THESE.
  //   Inputs
  //   Inputs/Outputs from run.circ. DO NOT MOVE THESE.
endmodule

module Branch_Comp (
  input  [31:0] r1,
  input  [31:0] r2,
  input  BrUn,
  output BrEq,
  output BrLT
);

  wire comparator_1_lt, comparator_2_lt;

  Comparator #(.width(32)) comparator_1 (.a(r1), .b(r2), .eq(BrEq), .lt(comparator_1_lt));  // open: gt
  Multiplexer #(.enable("false")) multiplexer_1 (.in0(comparator_1_lt), .in1(comparator_2_lt), .out(BrLT), .sel(BrUn));
  Comparator #(.width(32), .mode("unsigned")) comparator_2 (.a(r1), .b(r2), .lt(comparator_2_lt));  // open: gt, eq
endmodule

module Imm_Gen (
  input  [31:0] Instruction,
  input  [2:0] ImmSel,
  output [31:0] Imm
);

  wire [31:0] bit_extender_1_out, bit_extender_2_out, bit_extender_3_out, bit_extender_4_out;

  assign bit_extender_1_out = {{20{Instruction[31]}}, Instruction[31:20]};  // Bit_Extender bit_extender_1
  assign bit_extender_2_out = {{20{Instruction[31]}}, {Instruction[31:25], Instruction[11:7]}};  // Bit_Extender bit_extender_2
  assign bit_extender_3_out = {{19{Instruction[31]}}, {Instruction[31], Instruction[7], Instruction[30:25], Instruction[11:8], 1'b0}};  // Bit_Extender bit_extender_3
  assign bit_extender_4_out = {{11{Instruction[31]}}, {Instruction[31], Instruction[19:12], Instruction[20], Instruction[30:21], 1'b0}};  // Bit_Extender bit_extender_4
  Multiplexer #(.select(3), .width(32), .enable("false")) multiplexer_1 (
    .in0(bit_extender_1_out), .in1(bit_extender_2_out), .in2(bit_extender_3_out),
    .in3({Instruction[31:12], {12{1'b0}}}), .in4(bit_extender_4_out), .out(Imm), .sel(ImmSel));  // open: in5, in6, in7
endmodule

module Control (
  input  [31:0] Inst,
  input  BrEq,
  input  BrLT,
  output PCSel,
  output [2:0] ImmSel,
  output [3:0] ALUSel,
  output RegWEn,
  output [1:0] MemRW,
  output BrUn,
  output [1:0] WBSel,
  output ASel,
  output BSel,
  output kill,
  output Auipc,
  output B_load,
  output H_load,
  output U_load
);

  wire and_5_out, and_6_out, and_7_out, and_8_out, and_9_out, and_10_out, and_11_out, and_12_out, FC3_0,
       FC3_1, FC3_2, FC3_3, FC3_4, FC3_5, FC3_6, FC3_7, FC7_00, FC7_01, FC7_20, i_addi, i_andi, i_jalr, i_lb,
       i_lbu, i_lh, i_lhu, i_lw, i_ori, i_slli, i_slti, i_srai, i_srli, i_xori, Itype, Itype_jalr,
       Itype_load, Lui, not_1_out, not_2_out, not_3_out, not_4_out, or_1_out, or_2_out, or_3_out, or_4_out,
       or_5_out, or_8_out, or_9_out, or_10_out, or_11_out, or_12_out, or_13_out, or_17_out, or_19_out, r_add,
       r_and, r_divu, r_mul, r_mulh, r_mulhu, r_or, r_remu, r_sll, r_slt, r_srl, r_sub, r_xor, Rtype, s_sw,
       sb_beq, sb_bgeu, sb_blt, sb_bltu, sb_bne, SBtype, Stype, u_auipc, u_lui, uj_jal, UJtype;
  wire [1:0] multiplexer_1_out, multiplexer_7_out;
  wire [2:0] multiplexer_11_out, multiplexer_13_out, multiplexer_15_out;
  wire [3:0] multiplexer_2_out, multiplexer_4_out, multiplexer_5_out, multiplexer_6_out, multiplexer_8_out,
       multiplexer_10_out, multiplexer_12_out, multiplexer_14_out, multiplexer_17_out, multiplexer_18_out,
       multiplexer_19_out, multiplexer_20_out, multiplexer_21_out;

  or or_1 (or_1_out, sb_blt, sb_bltu);
  not not_1 (not_1_out, BrEq);
  not not_2 (not_2_out, BrLT);
  or or_2 (or_2_out, r_or, i_ori);
  Multiplexer #(.width(2), .enable("false")) multiplexer_1 (
    .in0(2'b00), .in1(2'b01), .out(multiplexer_1_out), .sel(Stype));
  or or_3 (or_3_out, sb_blt, sb_bltu);
  not not_3 (not_3_out, BrEq);
  not not_4 (not_4_out, BrLT);
  and and_1 (s_sw, Stype, FC3_2);
  and and_2 (u_auipc, Auipc, 1'b1);
  and and_3 (u_lui, Lui, 1'b1);
  and and_4 (uj_jal, UJtype, 1'b1);
  and and_5 (and_5_out, sb_beq, BrEq);
  and and_6 (and_6_out, or_1_out, BrLT);
  and and_7 (and_7_out, sb_bne, not_1_out);
  and and_8 (and_8_out, sb_bgeu, not_2_out);
  Multiplexer #(.width(4), .enable("false")) multiplexer_2 (
    .in0(4'b0000), .in1(4'b0001), .out(multiplexer_2_out), .sel(or_2_out));
  or or_4 (or_4_out, r_xor, i_xori);
  Multiplexer #(.width(2), .enable("false")) multiplexer_3 (
    .in0(multiplexer_1_out), .in1(2'b10), .out(MemRW), .sel(or_5_out));
  or or_5 (or_5_out, Itype_load, SBtype, Lui, UJtype, Itype_jalr);
  and and_9 (and_9_out, sb_beq, BrEq);
  and and_10 (and_10_out, or_3_out, BrLT);
  and and_11 (and_11_out, sb_bne, not_3_out);
  and and_12 (and_12_out, sb_bgeu, not_4_out);
  Multiplexer #(.width(4), .enable("false")) multiplexer_4 (
    .in0(multiplexer_2_out), .in1(4'b0010), .out(multiplexer_4_out), .sel(or_4_out));
  or or_6 (kill, and_9_out, and_10_out, and_11_out, and_12_out, uj_jal, Itype_jalr);
  or or_7 (PCSel, and_5_out, and_6_out, and_7_out, and_8_out, uj_jal, Itype_jalr);
  Multiplexer #(.width(4), .enable("false")) multiplexer_5 (
    .in0(multiplexer_4_out), .in1(4'b0011), .out(multiplexer_5_out), .sel(or_8_out));
  or or_8 (or_8_out, r_add, i_addi, Itype_load, Itype_jalr, Stype, SBtype, Auipc, UJtype);
  Comparator #(.width(7)) comparator_1 (.a(Inst[6:0]), .b(7'b0110011), .eq(Rtype));  // open: gt, lt
  Comparator #(.width(7)) comparator_2 (.a(Inst[6:0]), .b(7'b0000011), .eq(Itype_load));  // open: gt, lt
  Comparator #(.width(7)) comparator_3 (.a(Inst[6:0]), .b(7'b1100111), .eq(Itype_jalr));  // open: gt, lt
  Comparator #(.width(7)) comparator_4 (.a(Inst[6:0]), .b(7'b0010011), .eq(Itype));  // open: gt, lt
  Comparator #(.width(7)) comparator_5 (.a(Inst[6:0]), .b(7'b0100011), .eq(Stype));  // open: gt, lt
  Comparator #(.width(7)) comparator_6 (.a(Inst[6:0]), .b(7'b1100011), .eq(SBtype));  // open: gt, lt
  Comparator #(.width(7)) comparator_7 (.a(Inst[6:0]), .b(7'b0010111), .eq(Auipc));  // open: gt, lt
  Comparator #(.width(7)) comparator_8 (.a(Inst[6:0]), .b(7'b0110111), .eq(Lui));  // open: gt, lt
  Comparator #(.width(7)) comparator_9 (.a(Inst[6:0]), .b(7'b1101111), .eq(UJtype));  // open: gt, lt
  and and_13 (sb_beq, SBtype, FC3_0);
  and and_14 (sb_blt, SBtype, FC3_4);
  and and_15 (sb_bltu, SBtype, FC3_6);
  and and_16 (sb_bne, SBtype, FC3_1);
  and and_17 (sb_bgeu, SBtype, FC3_7);
  or or_9 (or_9_out, Itype, Lui, Auipc, Rtype);
  Multiplexer #(.width(4), .enable("false")) multiplexer_6 (
    .in0(multiplexer_5_out), .in1(4'b0100), .out(multiplexer_6_out), .sel(r_sub));
  Multiplexer #(.width(2), .enable("false")) multiplexer_7 (
    .in0(2'b00), .in1(2'b01), .out(multiplexer_7_out), .sel(or_9_out));
  Multiplexer #(.width(4), .enable("false")) multiplexer_8 (
    .in0(multiplexer_6_out), .in1(4'b0101), .out(multiplexer_8_out), .sel(r_mul));
  Multiplexer #(.width(2), .enable("false")) multiplexer_9 (
    .in0(multiplexer_7_out), .in1(2'b10), .out(WBSel), .sel(or_11_out));
  or or_10 (or_10_out, Lui, Auipc);
  Multiplexer #(.width(4), .enable("false")) multiplexer_10 (
    .in0(multiplexer_8_out), .in1(4'b0110), .out(multiplexer_10_out), .sel(r_mulhu));
  or or_11 (or_11_out, Itype_jalr, UJtype);
  and and_18 (r_add, Rtype, FC3_0, FC7_00);
  and and_19 (r_mul, Rtype, FC3_0, FC7_01);
  and and_20 (r_sub, Rtype, FC3_0, FC7_20);
  and and_21 (r_sll, Rtype, FC3_1, FC7_00);
  and and_22 (i_lb, Itype_load, FC3_0);
  and and_23 (i_lh, Itype_load, FC3_1);
  and and_24 (i_lw, Itype_load, FC3_2);
  and and_25 (i_lbu, Itype_load, FC3_4);
  and and_26 (i_lhu, Itype_load, FC3_5);
  Multiplexer #(.width(3), .enable("false")) multiplexer_11 (
    .in0(3'b100), .in1(3'b011), .out(multiplexer_11_out), .sel(or_10_out));
  Multiplexer #(.width(4), .enable("false")) multiplexer_12 (
    .in0(multiplexer_10_out), .in1(4'b0111), .out(multiplexer_12_out), .sel(r_mulh));
  Multiplexer #(.width(3), .enable("false")) multiplexer_13 (
    .in0(multiplexer_11_out), .in1(3'b010), .out(multiplexer_13_out), .sel(SBtype));
  Multiplexer #(.width(4), .enable("false")) multiplexer_14 (
    .in0(multiplexer_12_out), .in1(4'b1000), .out(multiplexer_14_out), .sel(r_divu));
  Demultiplexer #(.select(3), .enable("false")) demultiplexer_1 (
    .out0(FC3_0), .out1(FC3_1), .out2(FC3_2), .out3(FC3_3), .out4(FC3_4), .out5(FC3_5), .out6(FC3_6),
    .out7(FC3_7), .in(1'b1), .sel(Inst[14:12]));
  Multiplexer #(.width(3), .enable("false")) multiplexer_15 (
    .in0(multiplexer_13_out), .in1(3'b001), .out(multiplexer_15_out), .sel(Stype));
  Multiplexer #(.width(3), .enable("false")) multiplexer_16 (
    .in0(multiplexer_15_out), .in1(3'b000), .out(ImmSel), .sel(or_12_out));
  or or_12 (or_12_out, Itype, Itype_load, Itype_jalr, Rtype);
  Multiplexer #(.width(4), .enable("false")) multiplexer_17 (
    .in0(multiplexer_14_out), .in1(4'b1001), .out(multiplexer_17_out), .sel(r_remu));
  or or_13 (or_13_out, r_srl, i_srli);
  or or_14 (B_load, i_lb, i_lbu);
  or or_15 (H_load, i_lh, i_lhu);
  or or_16 (U_load, i_lbu, i_lhu);
  and and_27 (r_mulh, Rtype, FC3_1, FC7_01);
  and and_28 (r_mulhu, Rtype, FC3_3, FC7_01);
  and and_29 (r_slt, Rtype, FC3_2, FC7_00);
  and and_30 (r_xor, Rtype, FC3_4, FC7_00);
  and and_31 (i_addi, Itype, FC3_0);
  and and_32 (i_slli, Itype, FC3_1, FC7_00);
  and and_33 (i_jalr, Itype_jalr, FC3_0);
  and and_34 (i_slti, Itype, FC3_2);
  Multiplexer #(.width(4), .enable("false")) multiplexer_18 (
    .in0(multiplexer_17_out), .in1(4'b1010), .out(multiplexer_18_out), .sel(or_13_out));
  Multiplexer #(.width(4), .enable("false")) multiplexer_19 (
    .in0(multiplexer_18_out), .in1(4'b1011), .out(multiplexer_19_out), .sel(i_srai));
  Multiplexer #(.width(4), .enable("false")) multiplexer_20 (
    .in0(multiplexer_19_out), .in1(4'b1100), .out(multiplexer_20_out), .sel(or_17_out));
  or or_17 (or_17_out, r_sll, i_slli);
  Comparator #(.width(7)) comparator_10 (.a(Inst[31:25]), .b({7{1'b0}}), .eq(FC7_00));  // open: gt, lt
  Comparator #(.width(7)) comparator_11 (.a(Inst[31:25]), .b(7'b0000001), .eq(FC7_01));  // open: gt, lt
  Comparator #(.width(7)) comparator_12 (.a(Inst[31:25]), .b(7'b0100000), .eq(FC7_20));  // open: gt, lt
  nor nor_1 (RegWEn, Stype, SBtype);
  or or_18 (ASel, Auipc, UJtype, SBtype);
  or or_19 (or_19_out, r_slt, i_slti);
  and and_35 (r_divu, Rtype, FC3_5, FC7_01);
  and and_36 (r_srl, Rtype, FC3_5, FC7_00);
  and and_37 (r_or, Rtype, FC3_6, FC7_00);
  and and_38 (r_remu, Rtype, FC3_7, FC7_01);
  and and_39 (i_xori, Itype, FC3_4);
  and and_40 (i_srli, Itype, FC3_5, FC7_00);
  and and_41 (i_srai, Itype, FC3_5, FC7_20);
  and and_42 (i_ori, Itype, FC3_6);
  Multiplexer #(.width(4), .enable("false")) multiplexer_21 (
    .in0(multiplexer_20_out), .in1(4'b1101), .out(multiplexer_21_out), .sel(or_19_out));
  Multiplexer #(.width(4), .enable("false")) multiplexer_22 (
    .in0(multiplexer_21_out), .in1(4'b1111), .out(ALUSel), .sel(u_lui));
  and and_43 (r_and, Rtype, FC3_7, FC7_00);
  and and_44 (i_andi, Itype, FC3_7);
  or or_20 (BrUn, sb_bltu, sb_bgeu);
  not not_5 (BSel, Rtype);

  // Other names for the same wires on the sheet: opcode[6:0] = Inst[6:0]; rd[4:0] = Inst[11:7];
  //   funct3[2:0] = Inst[14:12]; rs1[4:0] = Inst[19:15]; rs2[4:0] = Inst[24:20]; funct7[6:0] = Inst[31:25]
endmodule
