// Logisim project mem.circ as structural Verilog: 1 circuit, main circuit main
module main (
  input  [31:0] WriteAddr,
  input  [1:0] MemRW,
  input  clk,
  input  [31:0] WriteData,
  output [31:0] ReadData
);

  wire demultiplexer_1_out1, demultiplexer_1_out2;

  Demultiplexer #(.select(2), .enable("false")) demultiplexer_1 (
    .out1(demultiplexer_1_out1), .out2(demultiplexer_1_out2), .in(1'b1), .sel(MemRW));  // open: out0, out3
  RAM #(.addrWidth(16), .dataWidth(32), .trigger("falling"), .databus("bibus")) ram_1 (
    .addr(WriteAddr[15:0]), .we(demultiplexer_1_out1), .oe(demultiplexer_1_out2), .clk(clk), .din(WriteData),
    .dout(ReadData));
endmodule
